# Fritzing sketch thermistor_test_reading (saved by Fritzing 0.9.5d)
breadboards: 1

parts:
  R1 = Resistor [tolerance=±5% resistance=7500 package="0402 [SMD]"]
  R2 = Temperature Sensor (Thermistor) [thermistor_type=NTC package=THT]
  A1 = ESP32-pico-kit-v4 [part_number=ESP32--pico-kit-v4]
  R3 = Resistor [tolerance=±5% resistance=7500 package="0402 [SMD]"]
  R4 = Temperature Sensor (Thermistor) [thermistor_type=NTC package=THT]

nets:
  N1: R1.Pin_0, A1.Pin_19, A1.Pin_22, R3.Pin_1
  N2: R1.Pin_1, R2.pin_0, A1.Pin_12
  N3: R2.pin_1, A1.Pin_21, R4.pin_0
  N4: A1.Pin_26, R3.Pin_0, R4.pin_1

custom parts:
  ESP32-pico-kit-v4: ESP32-PICO-KIT is a mini development board produced by Espressif. At the core of this board is the ESP32-PICO-D4, a System-in-Package (SiP) module with complete Wi-Fi and Bluetooth functionalities.
